// Logisim project Computer1.circ as structural Verilog: 1 circuit, main circuit main
module main (
  input  [7:0] in_1,
  output out_2,
  output [7:0] out_3
);

  wire AC_p1, ALU_p12, and_1_out, decoder_1_out0, decoder_1_out1, decoder_1_out2, decoder_1_out3,
       decoder_1_out4, decoder_1_out5, decoder_1_out6, decoder_1_out7, decoder_2_out0, decoder_2_out1,
       decoder_2_out2, decoder_2_out3, decoder_2_out4, decoder_2_out5, decoder_2_out6, decoder_2_out7,
       decoder_2_out8, decoder_2_out9, decoder_2_out10, decoder_2_out11, decoder_2_out12, decoder_2_out13,
       decoder_2_out14, decoder_2_out15, FGI_Flag_q, FGO_Flag_q, I_Flag_out_4, IEN_Flag_q, main_1_add,
       main_1_and, main_1_clr_ac, main_1_clr_pc, main_1_clr_sc, main_1_com, main_1_dr, main_1_inpr,
       main_1_inr_ac, main_1_inr_ar, main_1_inr_dr, main_1_inr_pc, main_1_j_e, main_1_j_fgi, main_1_j_fgo,
       main_1_j_ien, main_1_j_r, main_1_j_s, main_1_k_e, main_1_k_fgi, main_1_k_fgo, main_1_k_ien,
       main_1_k_r, main_1_k_s, main_1_ld_ac, main_1_ld_ar, main_1_ld_dr, main_1_ld_ir, main_1_ld_outr,
       main_1_ld_pc, main_1_ld_tr, main_1_out_79, main_1_read, main_1_shl, main_1_shr, main_1_write,
       main_1_x1, main_1_x2, main_1_x3, main_1_x4, main_1_x5, main_1_x6, main_1_x7, not_1_out, not_2_out,
       or_1_out, or_2_out, OUTR_p3, PC_p6, R_Flag_q, S_Flag_q, TR_p5;
  wire [2:0] priority_encoder_1_out;
  wire [3:0] SC_out_3;
  wire [7:0] ALU_p10, bit_extender_3_out;
  wire [11:0] AR_p6, bit_extender_2_out;
  wire [15:0] ALU_p1, ALU_p11, bit_extender_1_out, bit_extender_4_out, IR_p5, ram_1_data, undriven;

  Bit_Extender #(.in_width(16)) bit_extender_1 (.in(bit_extender_4_out), .out(bit_extender_1_out));
  Bit_Extender #(.in_width(16), .out_width(12)) bit_extender_2 (.in(bit_extender_1_out), .out(bit_extender_2_out));
  Contol_Unit_main main_1 (
    .LD_AR(main_1_ld_ar), .out_79(main_1_out_79), .LD_IR(main_1_ld_ir), .x5(main_1_x5), .LD_DR(main_1_ld_dr),
    .INR_AR(main_1_inr_ar), .INR_DR(main_1_inr_dr), .x3(main_1_x3), .CLR_SC(main_1_clr_sc),
    .CLR_PC(main_1_clr_pc), .x4(main_1_x4), .x7(main_1_x7), .CLR_AC(main_1_clr_ac), .INR_AC(main_1_inr_ac),
    .INR_PC(main_1_inr_pc), .LD_OUTR(main_1_ld_outr), .J_IEN(main_1_j_ien), .K_IEN(main_1_k_ien),
    .K_FGI(main_1_k_fgi), .J_FGI(main_1_j_fgi), .K_FGO(main_1_k_fgo), .J_FGO(main_1_j_fgo), .K_S(main_1_k_s),
    .J_S(main_1_j_s), .J_R(main_1_j_r), .K_R(main_1_k_r), .I(I_Flag_out_4), .D7(decoder_1_out7),
    .D6(decoder_1_out6), .D5(decoder_1_out5), .D4(decoder_1_out4), .D3(decoder_1_out3), .D2(decoder_1_out2),
    .D1(decoder_1_out1), .D0(decoder_1_out0), .IR_10(IR_p5[11]), .IR_8(IR_p5[10]), .IR_9(IR_p5[9]),
    .IR_6(IR_p5[8]), .IR_7(IR_p5[7]), .IR_4(IR_p5[6]), .IR_5(IR_p5[5]), .in_50(IR_p5[4]), .IR_2(IR_p5[3]),
    .in_52(IR_p5[2]), .IR_0(IR_p5[1]), .T(IR_p5[0]), .T1(decoder_2_out1), .T2(decoder_2_out2),
    .T3(decoder_2_out3), .T4(decoder_2_out4), .T5(decoder_2_out5), .T6(decoder_2_out6), .T7(decoder_2_out7),
    .T8(decoder_2_out8), .T10(decoder_2_out9), .T12(decoder_2_out10), .T11(decoder_2_out11),
    .T14(decoder_2_out12), .T13(decoder_2_out13), .in_70(decoder_2_out14), .R(decoder_2_out15), .S(R_Flag_q),
    .in_73(S_Flag_q), .FGI(IEN_Flag_q), .in_75(FGI_Flag_q), .in_76(FGO_Flag_q), .LD_TR(main_1_ld_tr),
    .CLR_AR(ALU_p1[15]), .DR_13(ALU_p1[14]), .DR_11(ALU_p1[13]), .in_4(ALU_p1[12]), .DR_9(ALU_p1[11]),
    .in_6(ALU_p1[10]), .DR_7(ALU_p1[9]), .in_8(ALU_p1[8]), .DR_5(ALU_p1[7]), .in_10(ALU_p1[6]),
    .DR_3(ALU_p1[5]), .in_12(ALU_p1[4]), .DR_1(ALU_p1[3]), .in_14(ALU_p1[2]), .AC_15(ALU_p1[1]),
    .in_16(ALU_p1[0]), .AC_13(ALU_p11[15]), .in_18(ALU_p11[14]), .AC_11(ALU_p11[13]), .in_20(ALU_p11[12]),
    .AC_9(ALU_p11[11]), .in_22(ALU_p11[10]), .AC_7(ALU_p11[9]), .in_24(ALU_p11[8]), .AC_5(ALU_p11[7]),
    .in_26(ALU_p11[6]), .AC_3(ALU_p11[5]), .in_28(ALU_p11[4]), .AC_1(ALU_p11[3]), .in_30(ALU_p11[2]),
    .in_31(ALU_p11[1]), .E(ALU_p11[0]), .in_33(out_2), .x2(main_1_x2), .x6(main_1_x6), .Read(main_1_read),
    .Write(main_1_write), .J_E(main_1_j_e), .K_E(main_1_k_e), .T0(decoder_2_out0), .LD_AC(main_1_ld_ac),
    .LD_PC(main_1_ld_pc), .INPR(main_1_inpr), .COM(main_1_com), .SHL(main_1_shl), .AND(main_1_and),
    .ADD(main_1_add), .DR(main_1_dr), .SHR(main_1_shr), .x1(main_1_x1));  // open: T9
  Priority_Encoder priority_encoder_1 (
    .in1(main_1_x1), .in2(main_1_x2), .in3(main_1_x3), .in4(main_1_x4), .in5(main_1_x5), .in6(main_1_x6),
    .in7(main_1_x7), .out(priority_encoder_1_out));  // open: in0, en_in, gs, en_out
  Bit_Extender #(.in_width(16), .out_width(8)) bit_extender_3 (.in(bit_extender_1_out), .out(bit_extender_3_out));
  // OUTR_Register_main OUTR: pin names not known; wires that end beside it: bit_extender_3_out, main_1_ld_outr, OUTR_p3, out_3
  or or_1 (or_1_out, main_1_write, main_1_read);
  // ALU_COMP1_main ALU: pin names not known; wires that end beside it: ALU_p1, out_2, main_1_and, main_1_add, main_1_dr, main_1_inpr, main_1_com, main_1_shr, main_1_shl, ALU_p10, ALU_p11, ALU_p12
  Decoder #(.select(3), .enable("false")) decoder_1 (
    .out0(decoder_1_out0), .out1(decoder_1_out1), .out2(decoder_1_out2), .out3(decoder_1_out3),
    .out4(decoder_1_out4), .out5(decoder_1_out5), .out6(decoder_1_out6), .out7(decoder_1_out7),
    .sel(IR_p5[14:12]));
  Decoder #(.select(4), .enable("false")) decoder_2 (
    .out0(decoder_2_out0), .out1(decoder_2_out1), .out2(decoder_2_out2), .out3(decoder_2_out3),
    .out4(decoder_2_out4), .out5(decoder_2_out5), .out6(decoder_2_out6), .out7(decoder_2_out7),
    .out8(decoder_2_out8), .out9(decoder_2_out9), .out10(decoder_2_out10), .out11(decoder_2_out11),
    .out12(decoder_2_out12), .out13(decoder_2_out13), .out14(decoder_2_out14), .out15(decoder_2_out15),
    .sel(SC_out_3));
  // _12_bit_Register_main AR: pin names not known; wires that end beside it: bit_extender_2_out, main_1_out_79, main_1_inr_ar, main_1_ld_ar, OUTR_p3, AR_p6
  // _16_bit_Register_main IR: pin names not known; wires that end beside it: bit_extender_1_out, main_1_ld_ir, 1'b0, OUTR_p3, IR_p5
  I_Flag_main I_Flag (.in_1(IR_p5[15]), .in_2(not_2_out), .in_3(OUTR_p3), .out_4(I_Flag_out_4));
  SC_main SC (.out_3(SC_out_3), .in_2(OUTR_p3), .in_1(main_1_clr_sc));
  not not_1 (not_1_out, IR_p5[0]);
  and and_1 (and_1_out, not_1_out, main_1_j_s);
  RAM #(.addrWidth(12), .dataWidth(16), .bus("separate")) ram_1 (
    .addr(AR_p6), .din(bit_extender_1_out), .data(ram_1_data), .str(main_1_write), .sel(or_1_out),
    .clk(OUTR_p3), .ld(main_1_read));  // open: clr
  // _12_bit_Register_main PC: pin names not known; wires that end beside it: bit_extender_2_out, main_1_ld_pc, main_1_inr_pc, main_1_clr_pc, OUTR_p3, PC_p6
  // _16_bit_Register_main DR: pin names not known; wires that end beside it: bit_extender_1_out, main_1_ld_dr, main_1_inr_dr, OUTR_p3, ALU_p1
  // _16_bit_Register_main AC: pin names not known; wires that end beside it: AC_p1, AC_p1, main_1_ld_ac, main_1_inr_ac, main_1_clr_ac, OUTR_p3, ALU_p11
  // _16_bit_Register_main TR: pin names not known; wires that end beside it: bit_extender_1_out, main_1_ld_tr, 1'b0, OUTR_p3, TR_p5
  not not_2 (not_2_out, IR_p5[15]);
  J_K_Flip_Flop S_Flag (.J(and_1_out), .clk(OUTR_p3), .K(main_1_k_s), .Q(S_Flag_q));  // open: Qn, preset, en, reset
  J_K_Flip_Flop IEN_Flag (
    .J(main_1_j_ien), .clk(OUTR_p3), .K(main_1_k_ien), .Q(IEN_Flag_q));  // open: Qn, preset, en, reset
  J_K_Flip_Flop FGO_Flag (
    .J(main_1_j_fgo), .clk(OUTR_p3), .K(main_1_k_fgo), .Q(FGO_Flag_q));  // open: Qn, preset, en, reset
  J_K_Flip_Flop FGI_Flag (
    .J(main_1_j_fgi), .clk(OUTR_p3), .K(main_1_k_fgi), .Q(FGI_Flag_q));  // open: Qn, preset, en, reset
  J_K_Flip_Flop R_Flag (.J(main_1_j_r), .clk(OUTR_p3), .K(main_1_k_r), .Q(R_Flag_q));  // open: Qn, preset, en, reset
  Register INPR (.D(in_1), .Q(ALU_p10), .clk(OUTR_p3));  // open: en, clr
  or or_2 (or_2_out, ALU_p12, main_1_j_e);
  J_K_Flip_Flop E_Flag (.J(or_2_out), .clk(OUTR_p3), .K(main_1_k_e), .Q(out_2));  // open: Qn, preset, en, reset
  // _16_bit_common_bus_main main_2: pin names not known; wires that end beside it: ram_1_data, AR_p6, PC_p6, ALU_p1, ALU_p11, priority_encoder_1_out, undriven[15], undriven[14], undriven[13], undriven[12], undriven[11], undriven[10], undriven[9], undriven[8], undriven[7], undriven[6], undriven[5]
  Clock CLK (.out(OUTR_p3));
  Bit_Extender #(.in_width(16)) bit_extender_4 (.in(undriven), .out(bit_extender_4_out));

  // Notes on the sheet:
  //   Memory
  //   AR
  //   PC
  //   AC
  //   TR
  //   DR
endmodule
