// Logisim project I Flag.circ as structural Verilog: 1 circuit, main circuit main
module main (
  input  in_1,
  input  in_2,
  input  in_3,
  output out_4
);

  J_K_Flip_Flop j_k_ff_1 (.J(in_1), .clk(in_3), .K(in_2), .Q(out_4));  // open: Qn, preset, en, reset
endmodule
