// Logisim project SC.circ as structural Verilog: 1 circuit, main circuit main
module main (
  input  in_1,
  input  in_2,
  output [3:0] out_3
);

  Counter #(.width(4), .max('hf)) counter_1 (
    .D(4'b1111), .count(1'b1), .Q(out_3), .clk(in_2), .clr(in_1));  // open: load, carry
endmodule
